// Logisim project binary_to_dec_converter.circ as structural Verilog: 1 circuit, main circuit main
module main (
  input  A,
  input  B,
  input  C,
  input  D
);

  wire a_out, A_prime_B_prime_C_out, A_prime_B_prime_C_prime_D_prime_out, A_prime_B_prime_out,
       A_prime_BC_prime_D_out, A_prime_BC_prime_D_prime_out, A_prime_BC_prime_out, A_prime_BCD_out,
       A_prime_BCD_prime_out, A_prime_BD_out, A_prime_C_out, A_prime_CD_prime_out,
       AB_prime_C_prime_D_prime_out, AB_prime_C_prime_out, ACD_prime_out, b_out, c_out, C_prime_out, CD_out,
       d_out, e_out, f_out, g_out, not_1_out, not_2_out, not_3_out, not_4_out;

  not not_1 (not_1_out, A);
  not not_2 (not_2_out, B);
  not not_3 (not_3_out, C);
  not not_4 (not_4_out, D);
  and A_prime_B_prime (A_prime_B_prime_out, not_1_out, not_2_out);
  and A_prime_B_prime_C (A_prime_B_prime_C_out, not_1_out, not_2_out, C);
  and A_prime_B_prime_C_prime_D_prime (A_prime_B_prime_C_prime_D_prime_out, not_1_out, not_2_out, not_3_out, not_4_out);
  // AND_Gate A_prime_B_prime_C_prime_D has open pins: in0=not_1_out, in1=not_2_out, in2=not_3_out, in3=D, out=open
  and A_prime_BC_prime (A_prime_BC_prime_out, not_1_out, B, not_3_out);
  and A_prime_BC_prime_D_prime (A_prime_BC_prime_D_prime_out, not_1_out, B, not_3_out, not_4_out);
  and A_prime_BC_prime_D (A_prime_BC_prime_D_out, not_1_out, B, D, not_3_out);
  and A_prime_BCD_prime (A_prime_BCD_prime_out, not_1_out, B, C, not_4_out);
  and A_prime_BCD (A_prime_BCD_out, not_1_out, B, C, D);
  and A_prime_BD (A_prime_BD_out, not_1_out, B, D);
  and A_prime_C (A_prime_C_out, not_1_out, C);
  and A_prime_CD_prime (A_prime_CD_prime_out, not_1_out, C, not_4_out);
  and AB_prime_C_prime (AB_prime_C_prime_out, A, not_2_out, not_3_out);
  and AB_prime_C_prime_D_prime (AB_prime_C_prime_D_prime_out, A, not_2_out, not_3_out, not_4_out);
  and ACD_prime (ACD_prime_out, A, C, not_4_out);
  buf C_prime (C_prime_out, not_3_out);  // AND_Gate
  and CD (CD_out, C, D);
  or u_a (a_out, A_prime_C_out, AB_prime_C_prime_out, A_prime_BD_out, A_prime_B_prime_C_prime_D_prime_out);
  or u_b (b_out, A_prime_B_prime_out, A_prime_BC_prime_D_prime_out, A_prime_BCD_out, AB_prime_C_prime_out);
  or u_c (c_out, C_prime_out, CD_out, ACD_prime_out, A_prime_BCD_prime_out);
  or u_d (d_out, A_prime_B_prime_C_prime_D_prime_out, A_prime_B_prime_C_out, A_prime_BC_prime_D_out, A_prime_BCD_prime_out, AB_prime_C_prime_out);
  or e (e_out, A_prime_B_prime_C_prime_D_prime_out, A_prime_CD_prime_out, AB_prime_C_prime_D_prime_out);
  or f (f_out, A_prime_B_prime_C_prime_D_prime_out, A_prime_BC_prime_out, A_prime_BCD_prime_out, AB_prime_C_prime_out);
  or g (g_out, A_prime_B_prime_C_out, A_prime_BC_prime_out, A_prime_BCD_prime_out, AB_prime_C_prime_out);
  _7_Segment_Display u_7_segment_display_1 (
    .g(g_out), .f(f_out), .a(a_out), .b(b_out), .e(e_out), .d(d_out), .c(c_out));  // open: dp
endmodule
