// Logisim project MUX.circ as structural Verilog: 1 circuit, main circuit main
module main (
  input  I0,
  input  I1,
  input  I2,
  input  I3,
  input  A1,
  input  A2
);

  wire and_1_out, and_2_out, and_3_out, and_4_out, not_1_out, not_2_out, or_1_out;

  not not_1 (not_1_out, A1);
  not not_2 (not_2_out, A2);
  and and_1 (and_1_out, not_1_out, not_2_out, I0);
  and and_2 (and_2_out, A2, not_1_out, I1);
  and and_3 (and_3_out, A1, I2, not_2_out);
  and and_4 (and_4_out, I3, A1, A2);
  or or_1 (or_1_out, and_1_out, and_2_out, and_3_out, and_4_out, and_4_out);
  // Probe on or_1_out
endmodule
