// Logisim project CombinationalCircuit.circ as structural Verilog: 1 circuit, main circuit main
module main (
  input  b_3,
  input  b_2,
  input  b_1,
  input  b_0
);

  wire A_out, and_1_out, and_2_out, and_3_out, and_4_out, and_5_out, and_6_out, and_7_out, and_8_out,
       and_9_out, and_10_out, and_11_out, and_12_out, and_13_out, B_out, C_out, D_out, E_out, F_out, G_out,
       nb_0_out, nb_1_out, nb_2_out, or_1_out;

  // NOT_Gate nb_3 has open pins: in=b_3, out=open
  not nb_2 (nb_2_out, b_2);
  not nb_1 (nb_1_out, b_1);
  not nb_0 (nb_0_out, b_0);
  or or_1 (or_1_out, nb_0_out, b_1);
  and and_1 (and_1_out, nb_0_out, nb_2_out);
  and and_2 (and_2_out, b_2, b_0);
  and and_3 (and_3_out, b_1, b_0);
  and and_4 (and_4_out, nb_1_out, nb_0_out);
  and and_5 (and_5_out, b_0, nb_1_out, b_2);
  and and_6 (and_6_out, nb_0_out, b_1);
  and and_7 (and_7_out, or_1_out, nb_2_out);
  and and_8 (and_8_out, nb_0_out, b_1);
  and and_9 (and_9_out, nb_0_out, nb_2_out);
  and and_10 (and_10_out, nb_0_out, nb_1_out);
  and and_11 (and_11_out, nb_1_out, b_2);
  and and_12 (and_12_out, nb_0_out, b_1);
  and and_13 (and_13_out, b_1, nb_2_out);
  or A (A_out, and_1_out, and_2_out, b_1, b_3);
  or B (B_out, and_3_out, and_4_out, nb_2_out);
  or C (C_out, b_0, nb_1_out, b_2);
  or D (D_out, b_3, and_5_out, and_6_out, and_7_out);
  or E (E_out, and_8_out, and_9_out);
  or F (F_out, b_2, and_10_out, b_3);
  or G (G_out, and_11_out, and_12_out, and_13_out, b_3);
  _7_Segment_Display u_7_segment_display_1 (
    .g(G_out), .f(F_out), .a(A_out), .b(B_out), .e(E_out), .d(D_out), .c(C_out));  // open: dp
endmodule
