// Logisim project MultiplexerUsingGates.circ as structural Verilog: 1 circuit, main circuit main
module main (
  input  A1,
  input  A0,
  input  I0,
  input  I1,
  input  I2,
  input  I3
);

  wire and_1_out, and_2_out, and_3_out, and_4_out, nA0_out, nA1_out, or_1_out;

  not nA1 (nA1_out, A1);
  not nA0 (nA0_out, A0);
  and and_1 (and_1_out, nA0_out, nA1_out, I0);
  and and_2 (and_2_out, A0, nA1_out, I1);
  and and_3 (and_3_out, A1, nA0_out, I2);
  and and_4 (and_4_out, A1, A0, I3);
  or or_1 (or_1_out, and_1_out, and_2_out, and_3_out, and_4_out);
  LED Y (.in(or_1_out));
endmodule
